// Logisim project comp_architecture.circ as structural Verilog: 5 circuits, main circuit main
module main (
  input  in_1,
  input  [7:0] in_2,
  input  [19:0] in_3,
  input  [4:0] in_4,
  input  reset,
  output [15:0] out_6
);

  wire alu_zero, and_1_out, clock_1_out, control_unit_1_branch, control_unit_1_out_3, control_unit_1_out_4,
       control_unit_1_out_5, control_unit_1_out_6, control_unit_1_out_8, control_unit_1_out_9,
       control_unit_1_out_10;
  wire [2:0] alu_control_aluctr, control_unit_1_aluop;
  wire [3:0] multiplexer_3_out;
  wire [7:0] rom_1_data;
  wire [19:0] adder_1_out, adder_2_out, alu_y, bit_extender_2_out, bit_extender_3_out, counter_1_q,
       multiplexer_1_out, multiplexer_2_out, multiplexer_4_out, multiplexer_5_out, ram_1_data,
       registers_reg1output, registers_reg2output, shifter_1_out;
  wire [19:8] rom_1_data_2;

  Counter #(.width(20), .max('hfffff)) counter_1 (
    .D(multiplexer_1_out), .Q(counter_1_q), .clk(clock_1_out), .clr(reset));  // open: load, count, carry
  Clock clock_1 (.out(clock_1_out));
  assign out_6 = {{8{in_1}}, in_2};  // Bit_Extender bit_extender_1
  Adder #(.width(20)) adder_1 (.a(in_3), .b(counter_1_q), .out(adder_1_out));  // open: cin, cout
  Adder #(.width(20)) adder_2 (.a(adder_1_out), .b(shifter_1_out), .out(adder_2_out));  // open: cin, cout
  Multiplexer #(.width(20), .enable("false")) multiplexer_1 (
    .in0(adder_1_out), .in1(adder_2_out), .out(multiplexer_1_out), .sel(and_1_out));
  Shifter #(.width(20)) shifter_1 (.in(multiplexer_2_out), .\dist (in_4), .out(shifter_1_out));
  ROM #(.addrWidth(20), .dataWidth(20)) rom_1 (.addr(counter_1_q), .data({rom_1_data_2, rom_1_data}));  // open: sel
  control_unit control_unit_1 (
    .opcode(rom_1_data_2[19:16]), .Aluop(control_unit_1_aluop), .out_3(control_unit_1_out_3),
    .out_4(control_unit_1_out_4), .out_5(control_unit_1_out_5), .out_6(control_unit_1_out_6),
    .branch(control_unit_1_branch), .out_8(control_unit_1_out_8), .out_9(control_unit_1_out_9),
    .out_10(control_unit_1_out_10));
  assign bit_extender_2_out = {{12{1'b0}}, rom_1_data};  // Bit_Extender bit_extender_2
  assign bit_extender_3_out = {{12{rom_1_data[7]}}, rom_1_data};  // Bit_Extender bit_extender_3
  and and_1 (and_1_out, alu_zero, control_unit_1_out_8);
  alu_control alu_control (.func(rom_1_data[3:0]), .Aluopt(control_unit_1_aluop), .Aluctr(alu_control_aluctr));
  Multiplexer #(.width(20), .enable("false")) multiplexer_2 (
    .in0(bit_extender_2_out), .in1(bit_extender_3_out), .out(multiplexer_2_out), .sel(control_unit_1_out_9));
  Multiplexer #(.width(4), .enable("false")) multiplexer_3 (
    .in0(rom_1_data_2[11:8]), .in1(rom_1_data[7:4]), .out(multiplexer_3_out), .sel(control_unit_1_out_4));
  registers registers (
    .reg1Output(registers_reg1output), .reg2Output(registers_reg2output), .RegAdress(multiplexer_3_out),
    .writeData(multiplexer_5_out), .control_RW(control_unit_1_out_3), .clock(clock_1_out),
    .reg2(rom_1_data_2[11:8]), .reg1(rom_1_data_2[15:12]));
  Multiplexer #(.width(20), .enable("false")) multiplexer_4 (
    .in0(registers_reg2output), .in1(multiplexer_2_out), .out(multiplexer_4_out), .sel(control_unit_1_out_5));
  Alu alu (
    .B(multiplexer_4_out), .A(registers_reg1output), .Y(alu_y), .zero(alu_zero), .select(alu_control_aluctr));  // open: in_4
  RAM #(.addrWidth(20), .dataWidth(20), .bus("separate")) ram_1 (
    .addr(alu_y), .din(registers_reg2output), .data(ram_1_data), .str(control_unit_1_branch),
    .clk(clock_1_out), .ld(control_unit_1_out_10));  // open: sel, clr
  Multiplexer #(.width(20), .enable("false")) multiplexer_5 (
    .in0(alu_y), .in1(ram_1_data), .out(multiplexer_5_out), .sel(control_unit_1_out_6));

  // Notes on the sheet:
  //   pc
  //   contents of rom_1 (hex, n*v repeats v):
  //   0 1231 21305 10001
  //   func
  //   op
  //   control unit
endmodule

module alu_control (
  input  [3:0] func,
  input  [2:0] Aluopt,
  output [2:0] Aluctr
);

  Multiplexer #(.width(3), .enable("false")) multiplexer_1 (
    .in0(Aluopt), .in1(func[2:0]), .out(Aluctr), .sel(Aluopt[2]));

  // Notes on the sheet:
  //   agar 1 nbod 3 ragham aluopt mishe javab 
  //   agar aluopt avalesh 1 bod 3 ta ragham akhar
endmodule

module control_unit (
  input  [3:0] opcode,
  output [2:0] Aluop,
  output out_3,
  output out_4,
  output out_5,
  output out_6,
  output branch,
  output out_8,
  output out_9,
  output out_10
);

  wire not_1_out, not_2_out, not_3_out, not_4_out, not_5_out, not_6_out, not_7_out, not_8_out, not_9_out,
       not_10_out, not_11_out, not_12_out;

  not not_1 (not_1_out, opcode[3]);
  not not_2 (not_2_out, opcode[2]);
  not not_3 (not_3_out, opcode[1]);
  not not_4 (not_4_out, opcode[0]);
  not not_5 (not_5_out, opcode[3]);
  not not_6 (not_6_out, opcode[2]);
  not not_7 (not_7_out, opcode[1]);
  not not_8 (not_8_out, opcode[3]);
  not not_9 (not_9_out, opcode[2]);
  not not_10 (not_10_out, opcode[0]);
  not not_11 (not_11_out, opcode[3]);
  not not_12 (not_12_out, opcode[2]);
  and and_1 (Aluop[2], not_1_out, not_2_out, not_3_out, not_4_out);
  and and_2 (out_6, not_5_out, not_6_out, not_7_out, opcode[0]);
  and and_3 (branch, not_8_out, not_9_out, opcode[1], not_10_out);
  and and_4 (Aluop[1], not_11_out, not_12_out, opcode[1], opcode[0]);
  or or_1 (out_3, Aluop[2], out_6);
  or or_2 (out_5, out_6, branch);
  or or_3 (out_9, out_6, branch);
  or or_4 (Aluop[0], out_6, branch);

  assign out_4 = Aluop[2];
  assign out_8 = Aluop[1];
  assign out_10 = out_6;

  // Notes on the sheet:
  //   R-type
  //   lw
  //   sw
  //   beq
  //   RegWrite
  //   RegDst
  //   AluSrc
  //   MemToReg
  //   MemWite
  //   extOp
  //   memread
endmodule

module registers (
  input  [3:0] RegAdress,
  input  [19:0] writeData,
  input  control_RW,
  input  clock,
  input  [3:0] reg2,
  input  [3:0] reg1,
  output [19:0] reg1Output,
  output [19:0] reg2Output
);

  wire and_1_out, and_2_out, and_3_out, and_4_out, and_5_out, and_6_out, and_7_out, and_8_out, and_9_out,
       and_10_out, and_11_out, and_12_out, and_13_out, and_14_out, and_15_out, and_16_out, decoder_1_out0,
       decoder_1_out1, decoder_1_out2, decoder_1_out3, decoder_1_out4, decoder_1_out5, decoder_1_out6,
       decoder_1_out7, decoder_1_out8, decoder_1_out9, decoder_1_out10, decoder_1_out11, decoder_1_out12,
       decoder_1_out13, decoder_1_out14, decoder_1_out15;
  wire [19:0] register_1_q, register_2_q, register_3_q, register_4_q, register_5_q, register_6_q,
       register_7_q, register_8_q, register_9_q, register_10_q, register_11_q, register_12_q, register_13_q,
       register_14_q, register_15_q, register_16_q;

  Decoder #(.select(4), .enable("false")) decoder_1 (
    .out0(decoder_1_out0), .out1(decoder_1_out1), .out2(decoder_1_out2), .out3(decoder_1_out3),
    .out4(decoder_1_out4), .out5(decoder_1_out5), .out6(decoder_1_out6), .out7(decoder_1_out7),
    .out8(decoder_1_out8), .out9(decoder_1_out9), .out10(decoder_1_out10), .out11(decoder_1_out11),
    .out12(decoder_1_out12), .out13(decoder_1_out13), .out14(decoder_1_out14), .out15(decoder_1_out15),
    .sel(RegAdress));
  and and_1 (and_1_out, decoder_1_out0, control_RW);
  and and_2 (and_2_out, decoder_1_out1, control_RW);
  and and_3 (and_3_out, decoder_1_out2, control_RW);
  and and_4 (and_4_out, decoder_1_out3, control_RW);
  and and_5 (and_5_out, decoder_1_out4, control_RW);
  and and_6 (and_6_out, decoder_1_out5, control_RW);
  and and_7 (and_7_out, decoder_1_out6, control_RW);
  and and_8 (and_8_out, decoder_1_out7, control_RW);
  Register #(.width(20)) register_1 (.D(writeData), .Q(register_1_q), .clk(clock), .clr(and_1_out));  // open: en
  Register #(.width(20)) register_2 (.D(writeData), .Q(register_2_q), .clk(clock), .clr(and_2_out));  // open: en
  Register #(.width(20)) register_3 (.D(writeData), .Q(register_3_q), .clk(clock), .clr(and_3_out));  // open: en
  Register #(.width(20)) register_4 (.D(writeData), .Q(register_4_q), .clk(clock), .clr(and_4_out));  // open: en
  Register #(.width(20)) register_5 (.D(writeData), .Q(register_5_q), .clk(clock), .clr(and_5_out));  // open: en
  Register #(.width(20)) register_6 (.D(writeData), .Q(register_6_q), .clk(clock), .clr(and_6_out));  // open: en
  Register #(.width(20)) register_7 (.D(writeData), .Q(register_7_q), .clk(clock), .clr(and_7_out));  // open: en
  Register #(.width(20)) register_8 (.D(writeData), .Q(register_8_q), .clk(clock), .clr(and_8_out));  // open: en
  and and_9 (and_9_out, decoder_1_out8, control_RW);
  and and_10 (and_10_out, decoder_1_out9, control_RW);
  and and_11 (and_11_out, decoder_1_out10, control_RW);
  and and_12 (and_12_out, decoder_1_out11, control_RW);
  and and_13 (and_13_out, decoder_1_out12, control_RW);
  and and_14 (and_14_out, decoder_1_out13, control_RW);
  and and_15 (and_15_out, decoder_1_out14, control_RW);
  and and_16 (and_16_out, decoder_1_out15, control_RW);
  Register #(.width(20)) register_9 (.D(writeData), .Q(register_9_q), .clk(clock), .clr(and_9_out));  // open: en
  Register #(.width(20)) register_10 (.D(writeData), .Q(register_10_q), .clk(clock), .clr(and_10_out));  // open: en
  Register #(.width(20)) register_11 (.D(writeData), .Q(register_11_q), .clk(clock), .clr(and_11_out));  // open: en
  Register #(.width(20)) register_12 (.D(writeData), .Q(register_12_q), .clk(clock), .clr(and_12_out));  // open: en
  Register #(.width(20)) register_13 (.D(writeData), .Q(register_13_q), .clk(clock), .clr(and_13_out));  // open: en
  Register #(.width(20)) register_14 (.D(writeData), .Q(register_14_q), .clk(clock), .clr(and_14_out));  // open: en
  Register #(.width(20)) register_15 (.D(writeData), .Q(register_15_q), .clk(clock), .clr(and_15_out));  // open: en
  Register #(.width(20)) register_16 (.Q(register_16_q), .clk(clock), .clr(and_16_out));  // open: D, en
  Multiplexer #(.select(4), .width(20), .enable("false")) multiplexer_1 (
    .in0(register_1_q), .in1(register_2_q), .in2(register_3_q), .in3(register_4_q), .in4(register_5_q),
    .in5(register_6_q), .in6(register_7_q), .in7(register_8_q), .in8(register_9_q), .in9(register_10_q),
    .in10(register_11_q), .in11(register_12_q), .in12(register_13_q), .in13(register_14_q),
    .in14(register_15_q), .in15(register_16_q), .out(reg1Output), .sel(reg1));
  Multiplexer #(.select(4), .width(20), .enable("false")) multiplexer_2 (
    .in0(register_1_q), .in1(register_2_q), .in2(register_3_q), .in3(register_4_q), .in4(register_5_q),
    .in5(register_6_q), .in6(register_7_q), .in7(register_8_q), .in8(register_9_q), .in9(register_10_q),
    .in10(register_11_q), .in11(register_12_q), .in12(register_13_q), .in13(register_14_q),
    .in14(register_15_q), .in15(register_16_q), .out(reg2Output), .sel(reg2));
endmodule

module Alu (
  input  [2:0] select,
  input  [19:0] A,
  input  [19:0] B,
  input  [19:0] in_4,
  output [19:0] Y,
  output zero
);

  wire [19:0] adder_1_out, AND_out, divider_1_out, multiplier_1_out, OR_out, subtractor_1_out, XOR_out;

  Adder #(.width(20)) adder_1 (.a(A), .b(B), .out(adder_1_out));  // open: cin, cout
  Subtractor #(.width(20)) subtractor_1 (.a(A), .b(B), .out(subtractor_1_out));  // open: bin, bout
  Multiplier #(.width(20)) multiplier_1 (.a(A), .b(B), .out(multiplier_1_out));  // open: cin, cout
  Divider #(.width(20)) divider_1 (.a(A), .b(B), .out(divider_1_out));  // open: upper, rem
  assign AND_out = A & B;  // AND_Gate AND, 20 bits wide
  assign OR_out = A | B;  // OR_Gate OR, 20 bits wide
  assign XOR_out = A ^ B;  // XOR_Gate XOR, 20 bits wide
  Multiplexer #(.select(3), .width(20), .enable("false")) multiplexer_1 (
    .in0(in_4), .in1(adder_1_out), .in2(subtractor_1_out), .in3(multiplier_1_out), .in4(divider_1_out),
    .in5(AND_out), .in6(OR_out), .in7(XOR_out), .out(Y), .sel(select));
  nand Zero_Check (zero, Y[0], Y[1], Y[2], Y[3], Y[4], Y[5], Y[6], Y[7], Y[8], Y[9], Y[11], Y[12], Y[13], Y[14], Y[15], Y[16], Y[17], Y[18], Y[19]);
endmodule
